# Fritzing sketch rfid_with_shield (saved by Fritzing 0.9.2b)
breadboards: 1

parts:
  Part1 = RFID-RC522-v2
  Part2 = Arduino Uno (Rev3)
  R1 = Resistor [tolerance=±5% resistance=220 package=THT]
  LED1 = LED - 5mm [color="Green (555nm)" package="5 mm [THT]"]

nets:
  N1: Part1.NSS, Part2.D8
  N2: Part1.SCK, Part2.D13/SCK
  N3: Part1.MOSI, Part2.D11_PWM/MOSI
  N4: Part1.MISO, Part2.D12/MISO
  GND: Part1.GND, Part2.GND, R1.Pin_1
  N5: Part1.RST, Part2.D9_PWM
  VCC: Part1.VCC, Part2.3V3
  N6: Part2.D6_PWM, LED1.anode
  N7: R1.Pin_0, LED1.cathode

custom parts:
  RFID-RC522-v2: A simple China made RFID-RC522 Reader; do check the pin labels, as this is a MFRC522 based clone.

// code stored in the sketch: rfid-fitz.ino
/* From MFRC522 library
 *  Typical pin layout used:
 * -----------------------------------------------------------------------------------------
 *             MFRC522      Arduino       Arduino   Arduino    Arduino          Arduino
 *             Reader/PCD   Uno           Mega      Nano v3    Leonardo/Micro   Pro Micro
 * Signal      Pin          Pin           Pin       Pin        Pin              Pin
 * -----------------------------------------------------------------------------------------
 * RST/Reset   RST          9             5         D9         RESET/ICSP-5     RST
 * SPI SS      SDA(SS)      10            53        D10        10               10
 * SPI MOSI    MOSI         11 / ICSP-4   51        D11        ICSP-4           16
 * SPI MISO    MISO         12 / ICSP-1   50        D12        ICSP-1           14
 * SPI SCK     SCK          13 / ICSP-3   52        D13        ICSP-3           15
 * 
 * Added by Ramkumar Shankar
 * 30 August 2015
 * 
 * MFRC522 PIN     Arduino
 *                 Uno Pin
 * VCC             3V3   
 * GND             GND
 * 
 * 
 * LED connected to pin 6
 */

#include <SPI.h>
#include <MFRC522.h>

#define RST_PIN    9   // 
#define SS_PIN    10    //

MFRC522 mfrc522(SS_PIN, RST_PIN); // Create MFRC522 instance

int led = 7; //for LED

void setup() {
  // put your setup code here, to run once:
  //Initialize stuff needed for RFID reader
  Serial.begin(9600);   // Initialize serial communications with the PC
  while (!Serial);    // Do nothing if no serial port is opened (added for Arduinos based on ATMEGA32U4)
  SPI.begin();      // Init SPI bus
  mfrc522.PCD_Init();   // Init MFRC522
  ShowReaderDetails();  // Show details of PCD - MFRC522 Card Reader details
  Serial.println(F("Scan PICC to see UID, type, and data blocks..."));
  //Initialize onboard LED for feedback
  pinMode(led, OUTPUT);
}

void loop() {
  // Look for new cards
  if ( ! mfrc522.PICC_IsNewCardPresent()) {
    return;
  }

  // Select one of the cards
  if ( ! mfrc522.PICC_ReadCardSerial()) {
    return;
  }

  GetUID();
  digitalWrite(led, HIGH);
  Serial.println();
  delay(2000);
  digitalWrite(led, LOW);
}

void ShowReaderDetails() {
  // Get the MFRC522 software version
  byte v = mfrc522.PCD_ReadRegister(mfrc522.VersionReg);
  Serial.print(F("MFRC522 Software Version: 0x"));
  Serial.print(v, HEX);
  if (v == 0x91)
    Serial.print(F(" = v1.0"));
  else if (v == 0x92)
    Serial.print(F(" = v2.0"));
  else
    Serial.print(F(" (unknown)"));
  Serial.println("");
  // When 0x00 or 0xFF is returned, communication probably failed
  if ((v == 0x00) || (v == 0xFF)) {
    Serial.println(F("WARNING: Communication failure, is the MFRC522 properly connected?"));
  }
}

void GetUID () {
  for (byte i = 0; i < mfrc522.uid.size; i++) {
    Serial.print(mfrc522.uid.uidByte[i] < 0x10 ? " 0" : " ");
    Serial.print(mfrc522.uid.uidByte[i], HEX);
  }
}
